// Logisim project Pyotor_RAM_Controller_1.circ as structural Verilog: 1 circuit, main circuit main
module main (
);

  wire and_1_out, and_2_out, and_3_out, and_5_out, and_6_out, and_8_out, clock_1_out, clock_2_out,
       CLRSCR_out, comparator_1_eq, comparator_1_gt, ENABLE_p2, not_1_out, not_2_out, not_3_out, or_3_out,
       or_5_out, or_6_out, or_7_out, VIDEO_MASK_p2, VRAM_RESET_out, WRITE_p2, X_COUNTER_carry, X_RST_out,
       Y_COUNTER_carry, Y_RST_out;
  wire [7:0] ADDRESS_sw1, ADDRESS_sw9, and_4_out, and_9_out, bit_extender_1_out, bit_extender_2_out,
       DATA_IN_sw1, or_1_out, or_4_out, ram_1_dout, rom_1_data, VRAM_dout, X_COUNTER_q, Y_COUNTER_q;
  wire [15:0] and_7_out, bit_extender_3_out, counter_1_q, or_2_out;

  LED led_1 (.in(or_1_out[0]));
  LED led_2 (.in(or_1_out[1]));
  LED led_3 (.in(or_1_out[2]));
  DipSwitch #(.number(16)) ADDRESS (
    .sw1(ADDRESS_sw1[0]), .sw2(ADDRESS_sw1[1]), .sw3(ADDRESS_sw1[2]), .sw4(ADDRESS_sw1[3]),
    .sw5(ADDRESS_sw1[4]), .sw6(ADDRESS_sw1[5]), .sw7(ADDRESS_sw1[6]), .sw8(ADDRESS_sw1[7]),
    .sw9(ADDRESS_sw9[0]), .sw10(ADDRESS_sw9[1]), .sw11(ADDRESS_sw9[2]), .sw12(ADDRESS_sw9[3]),
    .sw13(ADDRESS_sw9[4]), .sw14(ADDRESS_sw9[5]), .sw15(ADDRESS_sw9[6]), .sw16(ADDRESS_sw9[7]));
  // Switch ENABLE: pin names not known; wires that end beside it: 1'b1, ENABLE_p2
  DipSwitch DATA_IN (
    .sw1(DATA_IN_sw1[0]), .sw2(DATA_IN_sw1[1]), .sw3(DATA_IN_sw1[2]), .sw4(DATA_IN_sw1[3]),
    .sw5(DATA_IN_sw1[4]), .sw6(DATA_IN_sw1[5]), .sw7(DATA_IN_sw1[6]), .sw8(DATA_IN_sw1[7]));
  LED led_4 (.in(or_1_out[3]));
  LED led_5 (.in(or_1_out[4]));
  LED led_6 (.in(or_1_out[5]));
  LED led_7 (.in(or_1_out[6]));
  LED led_8 (.in(or_1_out[7]));
  ROM rom_1 (.addr(ADDRESS_sw9), .data(rom_1_data));
  // Switch WRITE: pin names not known; wires that end beside it: 1'b1, WRITE_p2
  assign or_1_out = DATA_IN_sw1 | or_4_out;  // OR_Gate or_1, 8 bits wide
  Pull_Resistor pull_resistor_1 (.node(WRITE_p2));
  Pull_Resistor pull_resistor_2 (.node(ENABLE_p2));
  // Switch VIDEO_MASK: pin names not known; wires that end beside it: 1'b1, VIDEO_MASK_p2, rom_1_data[1], rom_1_data[2], rom_1_data[3], rom_1_data[4], rom_1_data[5], rom_1_data[6], rom_1_data[7]
  Pull_Resistor pull_resistor_3 (.node(VIDEO_MASK_p2));
  not not_1 (not_1_out, VIDEO_MASK_p2);
  and and_1 (and_1_out, rom_1_data[0], not_1_out);
  Clock #(.highDuration(5), .lowDuration(5)) clock_1 (.out(clock_1_out));
  and and_2 (and_2_out, and_1_out, WRITE_p2);
  and and_3 (and_3_out, and_1_out, ENABLE_p2);
  RAM #(.addrWidth(16)) ram_1 (
    .addr({ADDRESS_sw9, ADDRESS_sw1}), .we(and_2_out), .oe(and_3_out), .clk(clock_1_out), .din(DATA_IN_sw1),
    .dout(ram_1_dout));
  assign bit_extender_1_out = {{7{and_3_out}}, and_3_out};  // Bit_Extender bit_extender_1
  assign and_4_out = bit_extender_1_out & ram_1_dout;  // AND_Gate and_4, 8 bits wide
  assign or_2_out = {ADDRESS_sw9, ADDRESS_sw1} | and_7_out;  // OR_Gate or_2, 16 bits wide
  and and_5 (and_5_out, VIDEO_MASK_p2, WRITE_p2);
  and and_6 (and_6_out, VIDEO_MASK_p2, ENABLE_p2);
  or or_3 (or_3_out, and_6_out, not_2_out);
  not not_2 (not_2_out, clock_1_out);
  assign or_4_out = and_4_out | and_9_out;  // OR_Gate or_4, 8 bits wide
  Clock clock_2 (.out(clock_2_out));
  not not_3 (not_3_out, clock_1_out);
  assign and_7_out = bit_extender_3_out & counter_1_q;  // AND_Gate and_7, 16 bits wide
  RAM #(.addrWidth(16)) VRAM (
    .addr(or_2_out), .we(and_5_out), .oe(or_3_out), .clk(clock_1_out), .din(DATA_IN_sw1), .dout(VRAM_dout));
  and and_8 (and_8_out, clock_2_out, not_3_out);
  assign bit_extender_2_out = {{7{and_6_out}}, and_6_out};  // Bit_Extender bit_extender_2
  Counter #(.max('hffff), .width(16)) counter_1 (
    .Q(counter_1_q), .clk(and_8_out), .clr(or_5_out));  // open: load, D, count, carry, up
  assign bit_extender_3_out = {{15{and_8_out}}, and_8_out};  // Bit_Extender bit_extender_3
  assign and_9_out = bit_extender_2_out & VRAM_dout;  // AND_Gate and_9, 8 bits wide
  or or_5 (or_5_out, Y_COUNTER_carry, or_6_out);
  Button VRAM_RESET (.out(VRAM_RESET_out));
  Button Y_RST (.out(Y_RST_out));
  Counter Y_COUNTER (
    .count(X_COUNTER_carry), .Q(Y_COUNTER_q), .carry(Y_COUNTER_carry), .clk(and_8_out), .clr(Y_RST_out));  // open: load, D, up
  Button CLRSCR (.out(CLRSCR_out));
  Button X_RST (.out(X_RST_out));
  Counter X_COUNTER (
    .count(1'b1), .Q(X_COUNTER_q), .carry(X_COUNTER_carry), .clk(and_8_out), .clr(X_RST_out));  // open: load, D, up
  Comparator #(.mode("unsigned"), .width(16)) comparator_1 (
    .a(counter_1_q), .b(16'h3e80), .gt(comparator_1_gt), .eq(comparator_1_eq));  // open: lt
  or or_6 (or_6_out, comparator_1_gt, or_7_out);
  // RGB_Video #(.cursor("No Cursor"), .height(256), .reset("Synchronous"), .scale(1), .width(256)) rgb_video_1: pin names not known; wires that end beside it: CLRSCR_out, and_8_out, and_8_out, X_COUNTER_q, Y_COUNTER_q, VRAM_dout
  or or_7 (or_7_out, comparator_1_eq, VRAM_RESET_out);

  // Notes on the sheet:
  //   contents of rom_1 (hex, n*v repeats v):
  //   1 1
endmodule
